# Fritzing sketch Mega2560 schematics - Fritzing (saved by Fritzing 0.9.3b)
breadboards: 1

parts:
  Mega2560 = Arduino Mega 2560 (Rev3)
  S1 = Round Pushbutton
  S2 = Round Pushbutton
  S3 = Round Pushbutton
  S4 = Round Pushbutton
  S5 = Round Pushbutton
  S7 = Round Pushbutton
  S8 = Round Pushbutton
  U1 = POT [package=pot_mammoth]
  IC1 = ULN2003A [package="DIP16 [THT]"]
  U2 = POT [package=pot_mammoth]
  U3 = POT [package=pot_mammoth]
  U4 = POT [package=pot_mammoth]
  S9 = Round Pushbutton
  S10 = Round Pushbutton
  S11 = Round Pushbutton
  S12 = Round Pushbutton
  LAMPS = Camdenboss CTB0158-6 [part_number=CTB0158-6 package=THT]
  S6 = Round Pushbutton
  DRIVEBOARD_RX = Header 8 [package=bm08b-srss-tb]

nets:
  N1: Mega2560.A0, U1.S
  N2: Mega2560.A1, U2.S
  N3: Mega2560.A2, U3.S
  N4: Mega2560.A3, U4.S
  N5: Mega2560.A4, S11.leg0
  N6: Mega2560.A5, S12.leg0
  GND: Mega2560.GND, S7.leg1, S8.leg1, U1.A, IC1.0V, U2.A, U3.A, U4.A, S9.leg1, S10.leg1, S11.leg1, S12.leg1
  N7: Mega2560.D12_PWM, S1.leg0
  N8: Mega2560.D8_PWM, S2.leg0
  N9: Mega2560.5V, U1.E, IC1.COM_-_Common, U2.E, U3.E, U4.E
  N10: Mega2560.D0_RX0, S10.leg0
  N11: Mega2560.D1_TX0, S9.leg0
  N12: Mega2560.D2_PWM, S7.leg0
  N13: Mega2560.D3_PWM, S8.leg0
  N14: Mega2560.D4_PWM, S6.leg0
  N15: Mega2560.D5_PWM, S5.leg0
  N16: Mega2560.D6_PWM, S4.leg0
  N17: Mega2560.D7_PWM, S3.leg0
  N18: Mega2560.D22, DRIVEBOARD_RX.1
  N19: Mega2560.D23, DRIVEBOARD_RX.2
  N20: Mega2560.D24, DRIVEBOARD_RX.3
  N21: Mega2560.D25, DRIVEBOARD_RX.4
  N22: Mega2560.D26, DRIVEBOARD_RX.5
  N23: Mega2560.D27, DRIVEBOARD_RX.6
  N24: Mega2560.D28, DRIVEBOARD_RX.7
  N25: Mega2560.D29, DRIVEBOARD_RX.8
  N26: Mega2560.D38, IC1.In_1
  N27: Mega2560.D39, IC1.In_2
  N28: Mega2560.D50, IC1.In_3
  N29: Mega2560.D51, IC1.In_4
  N30: Mega2560.D52, IC1.In_5
  N31: Mega2560.D53, IC1.In_6
  N32: S1.leg1, S2.leg1, S3.leg1, S4.leg1, S5.leg1, S6.leg1
  N33: IC1.Out_6, LAMPS.pin6
  N34: IC1.Out_5, LAMPS.pin5
  N35: IC1.Out_4, LAMPS.pin4
  N36: IC1.Out_3, LAMPS.pin3
  N37: IC1.Out_2, LAMPS.pin2
  N38: IC1.Out_1, LAMPS.pin1

notes:
  To DRIVEBOARD RX
  Lamps
  Accel
  Brake
  Clutch
  Wheel
