# Fritzing sketch Leonardo PWM2M2 schematics - Fritzing (saved by Fritzing 0.9.3b)
breadboards: 1

parts:
  S1 = Round Pushbutton
  S2 = Round Pushbutton
  S3 = Round Pushbutton
  S4 = Round Pushbutton
  S5 = Round Pushbutton
  S7 = Round Pushbutton
  S8 = Round Pushbutton
  U1 = POT [package=pot_mammoth]
  U2 = POT [package=pot_mammoth]
  U3 = POT [package=pot_mammoth]
  U4 = POT [package=pot_mammoth]
  S11 = Round Pushbutton
  S12 = Round Pushbutton
  S6 = Round Pushbutton
  Leonardo = Arduino Leonardo (Rev3b)
  Pro_mini/micro = Arduino Pro Mini v13

nets:
  N1: S1.leg0, Leonardo.D12/A11
  GND: S1.leg1, S2.leg1, S3.leg1, S4.leg1, S5.leg1, S7.leg1, S8.leg1, U1.A, U2.A, U3.A, U4.A, S11.leg1, S12.leg1, S6.leg1, Leonardo.GND, Pro_mini/micro.GND
  N2: S2.leg0, Leonardo.D8/A8
  N3: S3.leg0, Leonardo.D7
  N4: S4.leg0, Leonardo.D6_PWM/A7
  N5: S5.leg0, Leonardo.D5_PWM
  N6: S7.leg0, Leonardo.D3_PWM/SCL, Leonardo.SCL
  N7: S8.leg0, Leonardo.D2/SDA
  N8: U1.S, Leonardo.A0
  N9: U1.E, U2.E, U3.E, U4.E, Leonardo.5V
  N10: U2.S, Leonardo.A1
  N11: U3.S, Leonardo.A2
  N12: U4.S, Leonardo.A3
  N13: S11.leg0, Leonardo.A5
  N14: S12.leg0, Leonardo.A4
  N15: S6.leg0, Leonardo.D4/A6
  N16: Leonardo.D1/TX, Pro_mini/micro.D1/RX

notes:
  PWM2M2
  Accel
  Brake
  Clutch
  Wheel
  A0 (POT. CENTER PIN)
  A1 (POT. CENTER PIN)
  A2 (POT. CENTER PIN)
  A3 (POT. CENTER PIN)
  Pro Mini
