# Fritzing sketch Leonardo schematics - Fritzing (saved by Fritzing 0.9.3b)
breadboards: 1

parts:
  S1 = Round Pushbutton
  S2 = Round Pushbutton
  S3 = Round Pushbutton
  S4 = Round Pushbutton
  S5 = Round Pushbutton
  S7 = Round Pushbutton
  S8 = Round Pushbutton
  U1 = POT [package=pot_mammoth]
  U2 = POT [package=pot_mammoth]
  U3 = POT [package=pot_mammoth]
  U4 = POT [package=pot_mammoth]
  S9 = Round Pushbutton
  S10 = Round Pushbutton
  S11 = Round Pushbutton
  S12 = Round Pushbutton
  S6 = Round Pushbutton
  Leonardo = Arduino Leonardo (Rev3b)
  DRIVER = Header 3 [package=1x03-1mm-ra]

nets:
  N1: S1.leg0, Leonardo.D12/A11
  GND: S1.leg1, S2.leg1, S3.leg1, S4.leg1, S5.leg1, S7.leg1, S8.leg1, U1.A, U2.A, U3.A, U4.A, S9.leg1, S10.leg1, S11.leg1, S12.leg1, S6.leg1, Leonardo.GND
  N2: S2.leg0, Leonardo.D8/A8
  N3: S3.leg0, Leonardo.D7
  N4: S4.leg0, Leonardo.D6_PWM/A7
  N5: S5.leg0, Leonardo.D5_PWM
  N6: S7.leg0, Leonardo.D3_PWM/SCL, Leonardo.SCL
  N7: S8.leg0, Leonardo.D2/SDA
  N8: U1.S, Leonardo.A0
  N9: U1.E, U2.E, U3.E, U4.E, Leonardo.5V
  N10: U2.S, Leonardo.A1
  N11: U3.S, Leonardo.A2
  N12: U4.S, Leonardo.A3
  N13: S9.leg0, Leonardo.D1/TX
  N14: S10.leg0, Leonardo.D0/RX
  N15: S11.leg0, Leonardo.A5
  N16: S12.leg0, Leonardo.A4
  N17: S6.leg0, Leonardo.D4/A6
  N18: Leonardo.D9_PWM/A9, DRIVER.3
  N19: Leonardo.D10_PWM/A10, DRIVER.2
  N20: Leonardo.D11_PWM, DRIVER.1

notes:
  MOTOR DRIVER (DC/Brushless)
  Accel
  Brake
  Clutch
  Wheel
  D9=PWM/PWM+
  D11=Reverse/Enable
  D10=Forward/PWM-
